// Logisim project Hammingcode.circ as structural Verilog: 1 circuit, main circuit main
module main (
  input  in_1,
  input  in_2,
  input  in_3,
  input  in_4,
  input  in_5,
  input  in_6,
  input  in_7,
  input  in_8,
  input  in_9,
  input  in_10,
  input  in_11,
  input  in_12,
  input  in_13,
  input  in_14,
  input  in_15,
  input  in_16,
  input  in_17,
  input  in_18,
  input  in_19,
  input  in_20,
  input  in_21,
  input  in_22
);

  wire and_1_out, and_2_out, and_3_out, and_4_out, and_5_out, and_6_out, and_7_out, and_8_out, not_1_out,
       not_2_out, not_3_out, not_4_out, not_5_out, not_6_out, xor_1_out, xor_2_out, xor_3_out, xor_4_out,
       xor_5_out, xor_6_out, xor_7_out, xor_8_out, xor_9_out, xor_10_out, xor_11_out, xor_12_out, xor_13_out,
       xor_14_out, xor_15_out, xor_16_out, xor_17_out, xor_18_out, xor_19_out, xor_20_out, xor_21_out,
       xor_22_out, xor_23_out, xor_24_out, xor_25_out, xor_26_out, xor_27_out;

  xor xor_1 (xor_1_out, in_3, in_6, in_10);
  xor xor_2 (xor_2_out, in_3, in_8, in_10);
  xor xor_3 (xor_3_out, in_6, in_8, in_10);
  xor xor_4 (xor_4_out, in_14, in_17, in_21);
  xor xor_5 (xor_5_out, in_14, in_19, in_21);
  xor xor_6 (xor_6_out, in_17, in_19, in_21);
  // Probe on xor_1_out
  // Probe on xor_2_out
  // Probe on in_3
  // Probe on xor_3_out
  // Probe on in_6
  // Probe on in_8
  // Probe on in_10
  // Probe on xor_4_out
  // Probe on xor_5_out
  // Probe on in_14
  // Probe on xor_6_out
  // Probe on in_17
  // Probe on in_19
  // Probe on in_21
  xor xor_7 (xor_7_out, xor_4_out, in_12);
  xor xor_8 (xor_8_out, xor_5_out, in_13);
  xor xor_9 (xor_9_out, in_14, in_15);
  xor xor_10 (xor_10_out, xor_6_out, in_16);
  xor xor_11 (xor_11_out, in_17, in_18);
  xor xor_12 (xor_12_out, in_19, in_20);
  xor xor_13 (xor_13_out, in_21, in_22);
  xor xor_14 (xor_14_out, in_1, in_4, in_7, in_11);
  xor xor_15 (xor_15_out, in_2, in_4, in_9, in_11);
  xor xor_16 (xor_16_out, in_5, in_7, in_9, in_11);
  xor xor_17 (xor_17_out, xor_7_out, xor_9_out, xor_11_out, xor_13_out);
  xor xor_18 (xor_18_out, xor_8_out, xor_9_out, xor_12_out, xor_13_out);
  xor xor_19 (xor_19_out, xor_10_out, xor_11_out, xor_12_out, xor_13_out);
  not not_1 (not_1_out, xor_16_out);
  not not_2 (not_2_out, xor_15_out);
  not not_3 (not_3_out, xor_14_out);
  not not_4 (not_4_out, xor_19_out);
  not not_5 (not_5_out, xor_18_out);
  not not_6 (not_6_out, xor_17_out);
  and and_1 (and_1_out, xor_14_out, xor_15_out, not_1_out);
  and and_2 (and_2_out, xor_14_out, not_2_out, xor_16_out);
  and and_3 (and_3_out, not_3_out, xor_15_out, xor_16_out);
  and and_4 (and_4_out, xor_14_out, xor_15_out, xor_16_out);
  and and_5 (and_5_out, xor_17_out, xor_18_out, not_4_out);
  and and_6 (and_6_out, xor_17_out, not_5_out, xor_19_out);
  and and_7 (and_7_out, not_6_out, xor_18_out, xor_19_out);
  and and_8 (and_8_out, xor_17_out, xor_18_out, xor_19_out);
  xor xor_20 (xor_20_out, and_1_out, in_4);
  // Probe on xor_20_out
  xor xor_21 (xor_21_out, and_2_out, in_7);
  // Probe on xor_21_out
  // Probe on xor_22_out
  xor xor_22 (xor_22_out, and_3_out, in_9);
  xor xor_23 (xor_23_out, and_4_out, in_11);
  // Probe on xor_23_out
  // Probe on xor_24_out
  xor xor_24 (xor_24_out, and_5_out, xor_9_out);
  xor xor_25 (xor_25_out, and_6_out, xor_11_out);
  // Probe on xor_25_out
  xor xor_26 (xor_26_out, and_7_out, xor_12_out);
  // Probe on xor_26_out
  xor xor_27 (xor_27_out, and_8_out, xor_13_out);
  // Probe on xor_27_out

  // Notes on the sheet:
  //   Кодирование
  //   Добавление ошибки
  //   Полная схема кодирования/декодирования
  //   Декодирование
endmodule
